// Logisim project lab3.circ as structural Verilog
module full_adder (
  input  X1,
  input  X2,
  input  X3,
  output P,
  output s
);

  wire _1_2_out, _1_out, _2_2_out, _3_out;

  xor _1 (_1_out, X1, X2);
  xor _2 (s, _1_out, X3);
  and _1_2 (_1_2_out, X1, X2);
  and _2_2 (_2_2_out, X1, X3);
  and _3 (_3_out, X2, X3);
  or or_1 (P, _2_2_out, _1_2_out, _3_out);
endmodule

module adder_8bit (
  input  A6,
  input  A1,
  input  A3,
  input  A4,
  input  A5,
  input  A0,
  input  A2,
  input  B0,
  input  B1,
  input  B2,
  input  B3,
  input  B4,
  input  B5,
  input  B6,
  input  A7,
  input  B7,
  output S6,
  output S4,
  output S2,
  output S5,
  output S1,
  output S3,
  output S0,
  output Cout,
  output S7
);

  wire full_adder_1_p, full_adder_2_p, full_adder_3_p, full_adder_4_p, full_adder_5_p, full_adder_6_p,
       full_adder_7_p;

  full_adder full_adder_1 (.X1(A0), .X2(B0), .X3(1'b0), .P(full_adder_1_p), .s(S0));
  full_adder full_adder_2 (.X1(A1), .X2(B1), .X3(full_adder_1_p), .P(full_adder_2_p), .s(S1));
  full_adder full_adder_3 (.X1(A2), .X2(B2), .X3(full_adder_2_p), .P(full_adder_3_p), .s(S2));
  full_adder full_adder_4 (.X1(A3), .X2(B3), .X3(full_adder_3_p), .P(full_adder_4_p), .s(S3));
  full_adder full_adder_5 (.X1(A4), .X2(B4), .X3(full_adder_4_p), .P(full_adder_5_p), .s(S4));
  full_adder full_adder_6 (.X1(A5), .X2(B5), .X3(full_adder_5_p), .P(full_adder_6_p), .s(S5));
  full_adder full_adder_7 (.X1(A6), .X2(B6), .X3(full_adder_6_p), .P(full_adder_7_p), .s(S6));
  full_adder full_adder_8 (.X1(A7), .X2(B7), .X3(full_adder_7_p), .P(Cout), .s(S7));
endmodule

module counter (
  output Q0,
  output Q1,
  output Q2
);

  wire clock_1_out, \и_out ;

  Clock clock_1 (.out(clock_1_out));
  T_Flip_Flop t_ff_1 (.clk(clock_1_out), .T(1'b1), .Q(Q0));  // open: Qn, preset, reset, en
  T_Flip_Flop t_ff_2 (.clk(clock_1_out), .T(Q0), .Q(Q1));  // open: Qn, preset, reset, en
  and \u_и  (\и_out , Q0, Q1);
  T_Flip_Flop t_ff_3 (.clk(clock_1_out), .T(\и_out ), .Q(Q2));  // open: Qn, preset, reset, en
endmodule
